# Fritzing sketch MiLightReceiver (saved by Fritzing 0.9.2b)
breadboards: 1

parts:
  Part1 = Arduino Uno (Rev3) - ICSP
  NRF24L1 = NRF24L01
  S1 = Pushbutton [package="[THT]"]
  R1 = Resistor [tolerance=±5% resistance=10k package=THT]

nets:
  N1: Part1.D8, NRF24L1.CE
  N2: Part1.D10_PWM/SS, NRF24L1.CSN
  N3: Part1.D11_PWM/MOSI, NRF24L1.MOSI
  N4: Part1.D12/MISO, NRF24L1.MISO
  N5: Part1.D13/SCK, NRF24L1.SCK
  N6: Part1.D2, S1.Pin_1, S1.Pin_2, R1.Pin_0
  3V3: Part1.3V3, NRF24L1.VCC
  N7: Part1.5V, S1.Pin_3, S1.Pin_4
  GND: Part1.GND, NRF24L1.GND, R1.Pin_1

custom parts:
  NRF24L01: NRF24L01 module
